// Logisim project CPU.circ as structural Verilog: 7 circuits, main circuit 1b LU
module _1b_LU (
  input  [1:0] S,
  input  A,
  input  B,
  output F
);

  wire and_1_out, nor_1_out, or_1_out, xor_1_out;

  and and_1 (and_1_out, A, B);
  or or_1 (or_1_out, A, B);
  xor xor_1 (xor_1_out, A, B);
  nor nor_1 (nor_1_out, A, B);
  Multiplexer #(.select(2)) multiplexer_1 (
    .in0(and_1_out), .in1(or_1_out), .in2(xor_1_out), .in3(nor_1_out), .out(F), .sel(S));  // open: en
endmodule

module _4b_ALU (
  input  [1:0] S,
  input  M,
  input  [3:0] A,
  input  [3:0] B,
  input  Cin,
  input  Less,
  output [3:0] F,
  output Zero,
  output Cout,
  output Overflow,
  output Set
);

  wire decoder_1_out3, decoder_1_out6, decoder_1_out8, decoder_1_out13, n1b_lu_1_f, n1b_lu_2_f, n1b_lu_3_f,
       n1b_lu_4_f;
  wire [2:0] n4b_au_1_f_2;
  wire [3:3] n4b_au_1_f;

  _1b_LU u_1b_lu_1 (.A(A[0]), .B(B[0]), .F(n1b_lu_1_f), .S(S));
  _1b_LU u_1b_lu_2 (.A(A[1]), .B(B[1]), .F(n1b_lu_2_f), .S(S));
  _1b_LU u_1b_lu_3 (.A(A[2]), .B(B[2]), .F(n1b_lu_3_f), .S(S));
  _1b_LU u_1b_lu_4 (.A(A[3]), .B(B[3]), .F(n1b_lu_4_f), .S(S));
  Multiplexer #(.select(2)) multiplexer_1 (
    .in0(n1b_lu_1_f), .in1(n1b_lu_1_f), .in2(n4b_au_1_f_2[0]), .in3(Less), .out(F[0]), .sel({M, S[1]}));  // open: en
  Multiplexer #(.select(2)) multiplexer_2 (
    .in0(n1b_lu_2_f), .in1(n1b_lu_2_f), .in2(n4b_au_1_f_2[1]), .in3(1'b0), .out(F[1]), .sel({M, S[1]}));  // open: en
  Multiplexer #(.select(2)) multiplexer_3 (
    .in0(n1b_lu_3_f), .in1(n1b_lu_3_f), .in2(n4b_au_1_f_2[2]), .in3(1'b0), .out(F[2]), .sel({M, S[1]}));  // open: en
  Multiplexer #(.select(2)) multiplexer_4 (
    .in0(n1b_lu_4_f), .in1(n1b_lu_4_f), .in2(n4b_au_1_f[3]), .in3(1'b0), .out(F[3]), .sel({M, S[1]}));  // open: en
  Decoder #(.select(4)) decoder_1 (
    .out3(decoder_1_out3), .out6(decoder_1_out6), .out8(decoder_1_out8), .out13(decoder_1_out13),
    .sel({n4b_au_1_f[3], B[3], A[3], S[0]}));  // open: out0, out1, out2, out4, out5, out7, out9, out10, out11, out12, out14, out15, en
  nor nor_1 (Zero, F[0], F[1], F[2], F[3]);
  _4b_AU u_4b_au_1 (.A(A), .B(B), .F({n4b_au_1_f[3], n4b_au_1_f_2}), .Cin(Cin), .Cout(Cout), .Sub(S[0]));
  or or_1 (Overflow, decoder_1_out3, decoder_1_out6, decoder_1_out8, decoder_1_out13);
  xor xor_1 (Set, Overflow, n4b_au_1_f[3]);
endmodule

module _4b_AU (
  input  Cin,
  input  Sub,
  input  [3:0] A,
  input  [3:0] B,
  output [3:0] F,
  output Cout
);

  wire [3:0] xor_1_out;

  xor xor_1 (xor_1_out[0], Sub, B[0]);
  xor xor_2 (xor_1_out[1], Sub, B[1]);
  xor xor_3 (xor_1_out[2], Sub, B[2]);
  xor xor_4 (xor_1_out[3], Sub, B[3]);
  Adder #(.width(4)) adder_1 (.a(A), .b(xor_1_out), .out(F), .cin(Cin), .cout(Cout));
endmodule

module _8b_ALU (
  input  [1:0] Sel,
  input  M,
  input  [7:0] A,
  input  [7:0] B,
  output [7:0] F,
  output Zero,
  output Overflow,
  output Cout
);

  wire n4b_alu_1_cout, n4b_alu_1_zero, n4b_alu_2_set, n4b_alu_2_zero;

  _4b_ALU u_4b_alu_1 (
    .A(A[3:0]), .B(B[3:0]), .F(F[3:0]), .S(Sel), .M(M), .Less(n4b_alu_2_set), .Cout(n4b_alu_1_cout),
    .Cin(Sel[0]), .Zero(n4b_alu_1_zero));  // open: Set, Overflow
  _4b_ALU u_4b_alu_2 (
    .A(A[7:4]), .B(B[7:4]), .F(F[7:4]), .S(Sel), .M(M), .Less(1'b0), .Set(n4b_alu_2_set), .Cout(Cout),
    .Cin(n4b_alu_1_cout), .Zero(n4b_alu_2_zero), .Overflow(Overflow));
  and and_1 (Zero, n4b_alu_1_zero, n4b_alu_2_zero);
endmodule

module CPU (
  input  [11:0] in_1,
  output [7:0] out_2,
  output [7:0] out_3,
  output [7:0] out_4
);

  wire Clock, decoder_1_out1, decoder_1_out2, decoder_1_out3, decoder_1_out4, decoder_1_out5, decoder_1_out6,
       decoder_1_out7, decoder_1_out8, decoder_1_out9, decoder_1_out10, decoder_1_out11, decoder_1_out12,
       decoder_1_out13, decoder_1_out14, decoder_1_out15, or_1_out, or_4_out;
  wire [1:0] or_2_out;
  wire [3:0] n4b_register_1_q;
  wire [7:0] multiplexer_1_out, ram_1_data;

  Button button_1 (.out(Clock));
  or or_1 (or_1_out, decoder_1_out8, decoder_1_out9, decoder_1_out10, decoder_1_out11, decoder_1_out12, decoder_1_out13, decoder_1_out14, decoder_1_out15);
  Multiplexer #(.width(8)) multiplexer_1 (
    .in0(out_3), .in1(ram_1_data), .out(multiplexer_1_out), .sel(or_1_out));  // open: en
  _4b_Register u_4b_register_1 (.D(in_1[11:8]), .Clock(Clock), .Q(n4b_register_1_q));  // open: Preset, Enable, Clear
  _8b_Register u_8b_register_1 (.D(multiplexer_1_out), .Clock(Clock), .Q(out_2));  // open: Preset, Enable, Clear
  _8b_Register u_8b_register_2 (.D(in_1[7:0]), .Clock(Clock), .Q(out_4));  // open: Preset, Enable, Clear
  Decoder #(.select(4)) decoder_1 (
    .out1(decoder_1_out1), .out2(decoder_1_out2), .out3(decoder_1_out3), .out4(decoder_1_out4),
    .out5(decoder_1_out5), .out6(decoder_1_out6), .out7(decoder_1_out7), .out8(decoder_1_out8),
    .out9(decoder_1_out9), .out10(decoder_1_out10), .out11(decoder_1_out11), .out12(decoder_1_out12),
    .out13(decoder_1_out13), .out14(decoder_1_out14), .out15(decoder_1_out15), .sel(n4b_register_1_q));  // open: out0, en
  or or_2 (or_2_out[0], decoder_1_out7, decoder_1_out5, decoder_1_out3, decoder_1_out1);
  or or_3 (or_2_out[1], decoder_1_out7, decoder_1_out6, decoder_1_out3, decoder_1_out2);
  or or_4 (or_4_out, decoder_1_out7, decoder_1_out6, decoder_1_out5, decoder_1_out4);
  _8b_ALU u_8b_alu_1 (.A(out_2), .B(out_4), .F(out_3), .Sel(or_2_out), .M(or_4_out));  // open: Zero, Cout, Overflow
  RAM ram_1 (.addr(out_4), .data(ram_1_data), .clk(Clock));  // open: sel, ld, clr
endmodule

module _4b_Register (
  input  [3:0] D,
  input  Clock,
  input  Preset,
  input  Enable,
  input  Clear,
  output [3:0] Q
);

  D_Flip_Flop d_ff_1 (.clk(Clock), .D(D[0]), .Q(Q[0]), .preset(Preset), .en(Enable), .reset(Clear));  // open: Qn
  D_Flip_Flop d_ff_2 (.clk(Clock), .D(D[1]), .Q(Q[1]), .preset(Preset), .en(Enable), .reset(Clear));  // open: Qn
  D_Flip_Flop d_ff_3 (.clk(Clock), .D(D[2]), .Q(Q[2]), .preset(Preset), .en(Enable), .reset(Clear));  // open: Qn
  D_Flip_Flop d_ff_4 (.clk(Clock), .D(D[3]), .Q(Q[3]), .preset(Preset), .en(Enable), .reset(Clear));  // open: Qn
endmodule

module _8b_Register (
  input  [7:0] D,
  input  Clock,
  input  Preset,
  input  Enable,
  input  Clear,
  output [7:0] Q
);

  _4b_Register u_4b_register_1 (.D(D[3:0]), .Clock(Clock), .Q(Q[3:0]), .Preset(Preset), .Enable(Enable), .Clear(Clear));
  _4b_Register u_4b_register_2 (.D(D[7:4]), .Clock(Clock), .Q(Q[7:4]), .Preset(Preset), .Enable(Enable), .Clear(Clear));
endmodule
